# Fritzing sketch If thing (saved by Fritzing 0.9.3b)
breadboards: 1

parts:
  Part1 = Photon
  PIR1 = PIR sensor
  R1 = Resistor [tolerance=±5% resistance=220 package=THT]
  R2 = Photocell (LDR) [package=THT]
  T1 = LM35 Temperature Sensor [package="TO92 [THT]"]
  U1 = mystery part, 3 pins [chip_label=?]

nets:
  N1: Part1.A0, R1.Pin_0, R2.pin_0
  N2: Part1.A1, T1.Vout
  GND: Part1.GND, PIR1.GND, R1.Pin_1, T1.GND, U1.pin1
  VIN: Part1.VIN, PIR1.VDD, U1.pin2
  N3: Part1.D0, PIR1.SIG
  N4: Part1.D3, U1.pin3
  N5: Part1.3V3, R2.pin_1, T1.+Vs
